// Logisim project adder4.circ as structural Verilog: 2 circuits, main circuit main
module main (
  input  [3:0] A,
  input  [3:0] B,
  input  Cin,
  output Cout,
  output [3:0] S
);

  wire adder1_1_cout, adder1_2_cout, adder1_3_cout;

  adder1 adder1_1 (.A(A[0]), .B(B[0]), .Cin(Cin), .S(S[0]), .Cout(adder1_1_cout));
  adder1 adder1_2 (.A(A[1]), .B(B[1]), .Cin(adder1_1_cout), .S(S[1]), .Cout(adder1_2_cout));
  adder1 adder1_3 (.A(A[2]), .B(B[2]), .Cin(adder1_2_cout), .S(S[2]), .Cout(adder1_3_cout));
  adder1 adder1_4 (.A(A[3]), .B(B[3]), .Cin(adder1_3_cout), .S(S[3]), .Cout(Cout));
endmodule

module adder1 (
  input  A,
  input  B,
  input  Cin,
  output S,
  output Cout
);

  wire and_1_out, and_2_out, xor_1_out;

  xor xor_1 (xor_1_out, A, B);
  xor xor_2 (S, xor_1_out, Cin);
  and and_1 (and_1_out, xor_1_out, Cin);
  and and_2 (and_2_out, B, A);
  or or_1 (Cout, and_1_out, and_2_out);
endmodule
