// Logisim project leftshift32_template.circ as structural Verilog: 1 circuit, main circuit LeftShift32
module LeftShift32 (
  input  [31:0] B,
  input  [4:0] Sa,
  input  Cin,
  output [31:0] C
);

  wire [0:0] bit_extender_6_out;
  wire [1:0] bit_extender_5_out;
  wire [3:0] bit_extender_4_out;
  wire [7:0] bit_extender_2_out;
  wire [15:0] bit_extender_1_out;
  wire [31:0] multiplexer_1_out, multiplexer_2_out, multiplexer_3_out, multiplexer_4_out;

  assign bit_extender_1_out = {{15{Cin}}, Cin};  // Bit_Extender bit_extender_1
  Multiplexer #(.width(32), .enable("false")) multiplexer_1 (
    .in0(B), .in1({B[15:0], bit_extender_1_out}), .out(multiplexer_1_out), .sel(Sa[4]));
  Bit_Extender #(.in_width(16), .out_width(8)) bit_extender_2 (.in(bit_extender_1_out), .out(bit_extender_2_out));
  Bit_Extender #(.in_width(16), .out_width(8)) bit_extender_3 (.in(bit_extender_1_out), .out(bit_extender_2_out));
  Multiplexer #(.width(32), .enable("false")) multiplexer_2 (
    .in0(multiplexer_1_out), .in1({multiplexer_1_out[23:0], bit_extender_2_out}), .out(multiplexer_2_out),
    .sel(Sa[3]));
  Bit_Extender #(.out_width(4)) bit_extender_4 (.in(bit_extender_2_out), .out(bit_extender_4_out));
  Multiplexer #(.width(32), .enable("false")) multiplexer_3 (
    .in0(multiplexer_2_out), .in1({multiplexer_2_out[27:0], bit_extender_4_out}), .out(multiplexer_3_out),
    .sel(Sa[2]));
  Bit_Extender #(.in_width(4), .out_width(2)) bit_extender_5 (.in(bit_extender_4_out), .out(bit_extender_5_out));
  Multiplexer #(.width(32), .enable("false")) multiplexer_4 (
    .in0(multiplexer_3_out), .in1({multiplexer_3_out[29:0], bit_extender_5_out}), .out(multiplexer_4_out),
    .sel(Sa[1]));
  Bit_Extender #(.in_width(2), .out_width(1)) bit_extender_6 (.in(bit_extender_5_out), .out(bit_extender_6_out[0]));
  Multiplexer #(.width(32), .enable("false")) multiplexer_5 (
    .in0(multiplexer_4_out), .in1({multiplexer_4_out[30:0], bit_extender_6_out[0]}), .out(C), .sel(Sa[0]));
endmodule
