// Logisim project p1_everything.circ as structural Verilog: 21 circuits, main circuit ALU32
module LeftShift32 (
  input  [31:0] B,
  input  [4:0] Sa,
  input  Cin,
  output [31:0] C
);

  wire [0:0] bit_extender_6_out;
  wire [1:0] bit_extender_5_out;
  wire [3:0] bit_extender_4_out;
  wire [7:0] bit_extender_2_out;
  wire [15:0] bit_extender_1_out;
  wire [31:0] multiplexer_1_out, multiplexer_2_out, multiplexer_3_out, multiplexer_4_out;

  assign bit_extender_1_out = {{15{Cin}}, Cin};  // Bit_Extender bit_extender_1
  Multiplexer #(.width(32), .enable("false")) multiplexer_1 (
    .in0(B), .in1({B[15:0], bit_extender_1_out}), .out(multiplexer_1_out), .sel(Sa[4]));
  Bit_Extender #(.in_width(16), .out_width(8)) bit_extender_2 (.in(bit_extender_1_out), .out(bit_extender_2_out));
  Bit_Extender #(.in_width(16), .out_width(8)) bit_extender_3 (.in(bit_extender_1_out), .out(bit_extender_2_out));
  Multiplexer #(.width(32), .enable("false")) multiplexer_2 (
    .in0(multiplexer_1_out), .in1({multiplexer_1_out[23:0], bit_extender_2_out}), .out(multiplexer_2_out),
    .sel(Sa[3]));
  Bit_Extender #(.out_width(4)) bit_extender_4 (.in(bit_extender_2_out), .out(bit_extender_4_out));
  Multiplexer #(.width(32), .enable("false")) multiplexer_3 (
    .in0(multiplexer_2_out), .in1({multiplexer_2_out[27:0], bit_extender_4_out}), .out(multiplexer_3_out),
    .sel(Sa[2]));
  Bit_Extender #(.in_width(4), .out_width(2)) bit_extender_5 (.in(bit_extender_4_out), .out(bit_extender_5_out));
  Multiplexer #(.width(32), .enable("false")) multiplexer_4 (
    .in0(multiplexer_3_out), .in1({multiplexer_3_out[29:0], bit_extender_5_out}), .out(multiplexer_4_out),
    .sel(Sa[1]));
  Bit_Extender #(.in_width(2), .out_width(1)) bit_extender_6 (.in(bit_extender_5_out), .out(bit_extender_6_out[0]));
  Multiplexer #(.width(32), .enable("false")) multiplexer_5 (
    .in0(multiplexer_4_out), .in1({multiplexer_4_out[30:0], bit_extender_6_out[0]}), .out(C), .sel(Sa[0]));
endmodule

module adder1 (
  input  A,
  input  B,
  input  Cin,
  output Sout,
  output Cout
);

  wire and_1_out, and_2_out, xor_1_out;

  xor xor_1 (xor_1_out, A, B);
  and and_1 (and_1_out, xor_1_out, Cin);
  and and_2 (and_2_out, A, B);
  xor xor_2 (Sout, xor_1_out, Cin);
  or or_1 (Cout, and_1_out, and_2_out);
endmodule

module adder4 (
  input  [3:0] A,
  input  [3:0] B,
  input  Cin,
  output Cout,
  output [3:0] Sout
);

  wire adder2_1_cout;

  adder2 adder2_1 (.A(A[1:0]), .B(B[1:0]), .Cin(Cin), .Cout(adder2_1_cout), .Sout(Sout[1:0]));
  adder2 adder2_2 (.A(A[3:2]), .B(B[3:2]), .Cin(adder2_1_cout), .Cout(Cout), .Sout(Sout[3:2]));
endmodule

module adder32 (
  input  [31:0] B,
  input  [31:0] A,
  input  Cin,
  output V,
  output [31:0] C
);

  wire adder16_1_cout;

  adder16 adder16_1 (.B(A[15:0]), .A(B[15:0]), .Cin(Cin), .Cout(adder16_1_cout), .Sout(C[15:0]));
  adder16v adder16v_1 (.B(A[31:16]), .A(B[31:16]), .Cin(adder16_1_cout), .V(V), .Sout(C[31:16]));
endmodule

module adder2 (
  input  [1:0] A,
  input  [1:0] B,
  input  Cin,
  output Cout,
  output [1:0] Sout
);

  wire adder1_1_cout;

  adder1 adder1_1 (.A(A[0]), .B(B[0]), .Cin(Cin), .Sout(Sout[0]), .Cout(adder1_1_cout));
  adder1 adder1_2 (.A(A[1]), .B(B[1]), .Cin(adder1_1_cout), .Sout(Sout[1]), .Cout(Cout));
endmodule

module adder8 (
  input  [7:0] B,
  input  [7:0] A,
  input  Cin,
  output Cout,
  output [7:0] Sout
);

  wire adder4_1_cout;

  adder4 adder4_1 (.A(A[3:0]), .B(B[3:0]), .Cin(Cin), .Cout(adder4_1_cout), .Sout(Sout[3:0]));
  adder4 adder4_2 (.A(A[7:4]), .B(B[7:4]), .Cin(adder4_1_cout), .Cout(Cout), .Sout(Sout[7:4]));
endmodule

module ALU32 (
  input  [31:0] A,
  input  [31:0] B,
  input  [3:0] Op,
  input  [4:0] Sa,
  output V,
  output [31:0] C
);

  wire adder32_1_v, and_1_out, and_3_out, multiplexer_2_out, not_2_out, not_4_out, not_5_out, not_6_out,
       or_2_out, or_all_1_cout, or_all_2_cout;
  wire [31:0] adder32_1_c, and_2_out, bit_extender_1_out, bit_extender_2_out, bit_extender_3_out,
       bit_extender_4_out, bitreverse_1_cout, bitreverse_2_cout, leftshift32_1_c, multiplexer_1_out,
       multiplexer_3_out, multiplexer_4_out, multiplexer_5_out, multiplexer_6_out, multiplexer_7_out,
       multiplexer_8_out, not_1_out, not_3_out, or_1_out, xor_1_out;

  or_all or_all_1 (.A(B), .Cout(or_all_1_cout));
  bitreverse bitreverse_1 (.Cin(B), .Cout(bitreverse_1_cout));
  Multiplexer #(.width(32), .enable("false")) multiplexer_1 (
    .in0(B), .in1(bitreverse_1_cout), .out(multiplexer_1_out), .sel(Op[2]));
  and and_1 (and_1_out, Op[0], Op[2]);
  assign and_2_out = A & B;  // AND_Gate and_2, 32 bits wide
  assign or_1_out = A | B;  // OR_Gate or_1, 32 bits wide
  assign xor_1_out = A ^ B;  // XOR_Gate xor_1, 32 bits wide
  assign not_1_out = ~B;  // NOT_Gate not_1, 32 bits wide
  Multiplexer #(.enable("false")) multiplexer_2 (.in0(Op[1]), .in1(B[31]), .out(multiplexer_2_out), .sel(and_1_out));
  not not_2 (not_2_out, or_all_1_cout);
  or_all or_all_2 (.A(xor_1_out), .Cout(or_all_2_cout));
  Multiplexer #(.width(32), .enable("false")) multiplexer_3 (
    .in0(B), .in1(not_1_out), .out(multiplexer_3_out), .sel(Op[2]));
  assign not_3_out = ~or_1_out;  // NOT_Gate not_3, 32 bits wide
  not not_4 (not_4_out, B[31]);
  Multiplexer #(.select(2), .width(32), .enable("false")) multiplexer_4 (
    .in0(and_2_out), .in1(or_1_out), .in2(xor_1_out), .in3(not_3_out), .out(multiplexer_4_out), .sel(Op[2:1]));
  and and_3 (and_3_out, not_4_out, or_all_1_cout);
  or or_2 (or_2_out, B[31], not_2_out);
  not not_5 (not_5_out, or_all_2_cout);
  adder32 adder32_1 (.B(multiplexer_3_out), .A(A), .Cin(Op[2]), .V(adder32_1_v), .C(adder32_1_c));
  LeftShift32 leftshift32_1 (.B(multiplexer_1_out), .Sa(Sa), .Cin(multiplexer_2_out), .C(leftshift32_1_c));
  assign bit_extender_1_out = {{31{1'b0}}, and_3_out};  // Bit_Extender bit_extender_1
  assign bit_extender_2_out = {{31{1'b0}}, or_2_out};  // Bit_Extender bit_extender_2
  assign bit_extender_3_out = {{31{1'b0}}, or_all_2_cout};  // Bit_Extender bit_extender_3
  assign bit_extender_4_out = {{31{1'b0}}, not_5_out};  // Bit_Extender bit_extender_4
  Multiplexer #(.select(2), .width(32), .enable("false")) multiplexer_5 (
    .in0(bit_extender_4_out), .in1(bit_extender_3_out), .in2(bit_extender_1_out), .in3(bit_extender_2_out),
    .out(multiplexer_5_out), .sel(Op[2:1]));
  bitreverse bitreverse_2 (.Cin(leftshift32_1_c), .Cout(bitreverse_2_cout));
  Multiplexer #(.width(32), .enable("false")) multiplexer_6 (
    .in0(leftshift32_1_c), .in1(bitreverse_2_cout), .out(multiplexer_6_out), .sel(Op[2]));
  Multiplexer #(.width(32), .enable("false")) multiplexer_7 (
    .in0(multiplexer_4_out), .in1(multiplexer_5_out), .out(multiplexer_7_out), .sel(Op[0]));
  Multiplexer #(.width(32), .enable("false")) multiplexer_8 (
    .in0(multiplexer_6_out), .in1(adder32_1_c), .out(multiplexer_8_out), .sel(Op[1]));
  Multiplexer #(.width(32), .enable("false")) multiplexer_9 (
    .in0(multiplexer_8_out), .in1(multiplexer_7_out), .out(C), .sel(Op[3]));
  not not_6 (not_6_out, Op[3]);
  and and_4 (V, adder32_1_v, Op[1], not_6_out);

  // Notes on the sheet:
  //   Op bit 1
  //   A
  //   Op bit 2
  //   B
  //   B
  //   B
  //   Op bit 2
  //   Op bit 1
  //   A EXOR B
  //   Mux 1
  //   Op Bit 2
  //   Mux 2
  //   Op Bit 0 and 2
  //   Op Bit 2
  //   Op bit 1
  //   Op bit 3
endmodule

module adder16 (
  input  [15:0] B,
  input  [15:0] A,
  input  Cin,
  output Cout,
  output [15:0] Sout
);

  wire adder8_1_cout;

  adder8 adder8_1 (.B(A[7:0]), .A(B[7:0]), .Cin(Cin), .Cout(adder8_1_cout), .Sout(Sout[7:0]));
  adder8 adder8_2 (.B(A[15:8]), .A(B[15:8]), .Cin(adder8_1_cout), .Cout(Cout), .Sout(Sout[15:8]));
endmodule

module adder2v (
  input  [1:0] A,
  input  [1:0] B,
  input  Cin,
  output V,
  output [1:0] Sout
);

  wire adder1_1_cout, adder1_2_cout;

  adder1 adder1_1 (.A(A[0]), .B(B[0]), .Cin(Cin), .Sout(Sout[0]), .Cout(adder1_1_cout));
  adder1 adder1_2 (.A(A[1]), .B(B[1]), .Cin(adder1_1_cout), .Sout(Sout[1]), .Cout(adder1_2_cout));
  xor xor_1 (V, adder1_1_cout, adder1_2_cout);
endmodule

module adder4v (
  input  [3:0] A,
  input  [3:0] B,
  input  Cin,
  output V,
  output [3:0] Sout
);

  wire adder2_1_cout;

  adder2 adder2_1 (.A(A[1:0]), .B(B[1:0]), .Cin(Cin), .Cout(adder2_1_cout), .Sout(Sout[1:0]));
  adder2v adder2v_1 (.A(A[3:2]), .B(B[3:2]), .Cin(adder2_1_cout), .V(V), .Sout(Sout[3:2]));
endmodule

module adder8v (
  input  [7:0] B,
  input  [7:0] A,
  input  Cin,
  output V,
  output [7:0] Sout
);

  wire adder4_1_cout;

  adder4 adder4_1 (.A(A[3:0]), .B(B[3:0]), .Cin(Cin), .Cout(adder4_1_cout), .Sout(Sout[3:0]));
  adder4v adder4v_1 (.A(A[7:4]), .B(B[7:4]), .Cin(adder4_1_cout), .V(V), .Sout(Sout[7:4]));
endmodule

module adder16v (
  input  [15:0] B,
  input  [15:0] A,
  input  Cin,
  output V,
  output [15:0] Sout
);

  wire adder8_1_cout;

  adder8 adder8_1 (.B(A[7:0]), .A(B[7:0]), .Cin(Cin), .Cout(adder8_1_cout), .Sout(Sout[7:0]));
  adder8v adder8v_1 (.B(A[15:8]), .A(B[15:8]), .Cin(adder8_1_cout), .V(V), .Sout(Sout[15:8]));
endmodule

module bitreverse (
  input  [31:0] Cin,
  output [31:0] Cout
);


  assign Cout = {Cin[0], Cin[1], Cin[2], Cin[3], Cin[4], Cin[5], Cin[6], Cin[7], Cin[8], Cin[9], Cin[10], Cin[11], Cin[12], Cin[13], Cin[14], Cin[15], Cin[16], Cin[17], Cin[18], Cin[19], Cin[20], Cin[21], Cin[22], Cin[23], Cin[24], Cin[25], Cin[26], Cin[27], Cin[28], Cin[29], Cin[30], Cin[31]};
endmodule

module Twoscomp (
  input  [31:0] A,
  input  [31:0] B,
  output [31:0] C
);

  assign C = ~(A | B);  // NOR_Gate nor_1, 32 bits wide
endmodule

module logicalor (
  input  [31:0] A,
  input  [31:0] B,
  output [31:0] C
);

  assign C = A | B;  // OR_Gate or_1, 32 bits wide
endmodule

module logicalnor (
  input  [31:0] A,
  input  [31:0] B,
  output [31:0] C
);

  assign C = ~(A | B);  // NOR_Gate nor_1, 32 bits wide
endmodule

module logicaland (
  input  [31:0] in_1,
  input  [31:0] in_2,
  output [31:0] out_3
);

  assign out_3 = in_1 & in_2;  // AND_Gate and_1, 32 bits wide
endmodule

module logicalxor (
  input  [31:0] in_1,
  input  [31:0] in_2,
  output [31:0] out_3
);

  assign out_3 = in_1 ^ in_2;  // XOR_Gate xor_1, 32 bits wide
endmodule

module le (
  input  [31:0] A,
  output C
);


  assign C = A[31];
endmodule

module gt (
  input  [31:0] A,
  output C
);

  not not_1 (C, A[31]);
endmodule

module or_all (
  input  [31:0] A,
  output Cout
);

  or or_1 (Cout, A[0], A[1], A[2], A[3], A[4], A[5], A[6], A[7], A[8], A[9], A[10], A[11], A[12], A[13], A[14], A[15], A[17], A[18], A[19], A[20], A[21], A[22], A[23], A[24], A[25], A[26], A[27], A[28], A[29], A[30], A[31], A[16]);
endmodule
