// Logisim project MIPS32.circ as structural Verilog: 14 circuits, main circuit MIPS32
module MIPS32 (
);

  wire clock_1_out, decode_1_lui_out, decode_1_movn_out, decode_1_movz_out, decode_1_shift_var,
       decode_1_slt_out, decode_1_sltu_out, decode_1_we, ex_mem_1_we_out, execute_1_we_out, id_ex_1_lui_out,
       id_ex_1_movn_out, id_ex_1_movz_out, id_ex_1_shift_var, id_ex_1_slt_out, id_ex_1_sltu_out,
       id_ex_1_we_out, mem_wb_1_we_out, memory_1_we_out, writeback_1_we_out;
  wire [3:0] decode_1_op_alu_out, id_ex_1_op_alu_out;
  wire [4:0] decode_1_ra, decode_1_rb, decode_1_rw, decode_1_sa_out, ex_mem_1_rw_out, execute_1_rw_out,
       id_ex_1_ra_out, id_ex_1_rb_out, id_ex_1_rw_out, id_ex_1_sa_out, mem_wb_1_rw_out, memory_1_rw_out,
       writeback_1_rw_out;
  wire [31:0] decode_1_a_out, decode_1_b_out, decode_1_ctrl_out, decode_1_lui_data_out, ex_mem_1_c_out,
       execute_1_c, fetch_1_word, forwarding_1_a_out, forwarding_1_b_out, id_ex_1_a_out, id_ex_1_b_out,
       id_ex_1_ctrl_out, id_ex_1_lui_data_out, if_id_1_word_out, mem_wb_1_c_out, mem_wb_1_data_out,
       memory_1_c_out, memory_1_data, writeback_1_c_out;

  Clock clock_1 (.out(clock_1_out));
  Fetch fetch_1 (.CLK(clock_1_out), .Word(fetch_1_word));
  IF_ID if_id_1 (.Word_in(fetch_1_word), .CLK(clock_1_out), .Word_out(if_id_1_word_out));
  Decode decode_1 (
    .C_In(writeback_1_c_out), .CLK(clock_1_out), .WE_in(writeback_1_we_out), .Word(if_id_1_word_out),
    .rW_in(writeback_1_rw_out), .A_out(decode_1_a_out), .LUI_Data_out(decode_1_lui_data_out),
    .B_out(decode_1_b_out), .Sa_out(decode_1_sa_out), .Ctrl_out(decode_1_ctrl_out), .WE(decode_1_we),
    .LUI_out(decode_1_lui_out), .Op_ALU_out(decode_1_op_alu_out), .SLT_out(decode_1_slt_out),
    .SLTU_out(decode_1_sltu_out), .rW(decode_1_rw), .rA(decode_1_ra), .rB(decode_1_rb),
    .MOVN_out(decode_1_movn_out), .MOVZ_out(decode_1_movz_out), .Shift_var(decode_1_shift_var));
  ID_EX id_ex_1 (
    .A_in(decode_1_a_out), .LUI_Data_in(decode_1_lui_data_out), .B_in(decode_1_b_out), .CLK(clock_1_out),
    .Sa_in(decode_1_sa_out), .SLT_in(decode_1_slt_out), .SLTU_in(decode_1_sltu_out),
    .LUI_in(decode_1_lui_out), .Ctrl_in(decode_1_ctrl_out), .Op_ALU_in(decode_1_op_alu_out),
    .rW_in(decode_1_rw), .rA(decode_1_ra), .rB(decode_1_rb), .WE(decode_1_we), .MOVN_in(decode_1_movn_out),
    .MOVZ_in(decode_1_movz_out), .Shift_var_in(decode_1_shift_var), .A_out(id_ex_1_a_out),
    .LUI_Data_out(id_ex_1_lui_data_out), .B_out(id_ex_1_b_out), .Sa_out(id_ex_1_sa_out),
    .SLT_out(id_ex_1_slt_out), .SLTU_out(id_ex_1_sltu_out), .LUI_out(id_ex_1_lui_out),
    .Ctrl_out(id_ex_1_ctrl_out), .Op_ALU_out(id_ex_1_op_alu_out), .rW_out(id_ex_1_rw_out),
    .rA_out(id_ex_1_ra_out), .rB_out(id_ex_1_rb_out), .WE_out(id_ex_1_we_out), .MOVN_out(id_ex_1_movn_out),
    .MOVZ_out(id_ex_1_movz_out), .Shift_var(id_ex_1_shift_var));
  Execute execute_1 (
    .A(forwarding_1_a_out), .B(forwarding_1_b_out), .LUI_Data(id_ex_1_lui_data_out), .LUI(id_ex_1_lui_out),
    .SLT(id_ex_1_slt_out), .Op_ALU(id_ex_1_op_alu_out), .Sa(id_ex_1_sa_out), .SLTU(id_ex_1_sltu_out),
    .Word_in(id_ex_1_ctrl_out), .rW(id_ex_1_rw_out), .WE_in(id_ex_1_we_out), .MOVN_in(id_ex_1_movn_out),
    .MOVZ_in(id_ex_1_movz_out), .Shift_var(id_ex_1_shift_var), .C(execute_1_c), .rW_out(execute_1_rw_out),
    .WE_out(execute_1_we_out));
  Forwarding forwarding_1 (
    .ID_EX_A(id_ex_1_a_out), .ID_EX_B(id_ex_1_b_out), .EX_MEM_Out(ex_mem_1_c_out),
    .MEM_WB_Out(mem_wb_1_c_out), .rA(id_ex_1_ra_out), .rB(id_ex_1_rb_out), .rD_EX_MEM(ex_mem_1_rw_out),
    .rD_MEM_WB(mem_wb_1_rw_out), .WE_EX_MEM(ex_mem_1_we_out), .WE_MEM_WB(mem_wb_1_we_out),
    .A_out(forwarding_1_a_out), .B_out(forwarding_1_b_out));
  EX_MEM ex_mem_1 (
    .CLK(clock_1_out), .C_in(execute_1_c), .rW(execute_1_rw_out), .WE_in(execute_1_we_out),
    .C_out(ex_mem_1_c_out), .rW_out(ex_mem_1_rw_out), .WE_out(ex_mem_1_we_out));
  Memory memory_1 (
    .C_in(ex_mem_1_c_out), .CLK(clock_1_out), .We_in(ex_mem_1_we_out), .rW(ex_mem_1_rw_out),
    .C_out(memory_1_c_out), .Data(memory_1_data), .WE_OUT(memory_1_we_out), .rW_out(memory_1_rw_out));
  MEM_WB mem_wb_1 (
    .CLK(clock_1_out), .C_in(memory_1_c_out), .Data_in(memory_1_data), .We_in(memory_1_we_out),
    .rW(memory_1_rw_out), .C_out(mem_wb_1_c_out), .Data_out(mem_wb_1_data_out), .We_out(mem_wb_1_we_out),
    .rW_out(mem_wb_1_rw_out));
  Writeback writeback_1 (
    .C_in(mem_wb_1_c_out), .Data(mem_wb_1_data_out), .WE_in(mem_wb_1_we_out), .rW(mem_wb_1_rw_out),
    .C_out(writeback_1_c_out), .We_out(writeback_1_we_out), .rW_out(writeback_1_rw_out));
endmodule

module Fetch (
  input  CLK,
  output [31:0] Word
);

  wire [29:0] incrementer_1_p2;
  wire [31:0] incrementer_1_p1;

  // Incrementer #(.width(30)) incrementer_1: pin names not known; wires that end beside it: incrementer_1_p1[31:2], incrementer_1_p2, incrementer_1_p1
  Register #(.width(32)) register_1 (
    .D({incrementer_1_p2, incrementer_1_p1[1:0]}), .en(CLK), .clk(CLK), .Q(incrementer_1_p1));  // open: clr
  // MIPSProgramROM mipsprogramrom_1: pin names not known; wires that end beside it: Word

  // Notes on the sheet:
  //   contents of mipsprogramrom_1 (hex, n*v repeats v):
  //   ADDIU $2, $zero, -26046 ADDIU $3, $zero, 5489 ADDIU $4, $zero, -9550 ADDIU $5, $zero, 23559 ADDIU
  //   $6, $zero, 15618 ADDIU $7, $zero, 26556 ADDIU $8, $zero, 12935 ADDIU $9, $zero, 1873 ADDIU $10,
  //   $zero, -23205 ADDIU $11, $zero, 18941 ADDIU $12, $zero, -32105 ADDIU $13, $zero, 31858 ADDIU $14,
  //   $zero, -27683 ADDIU $15, $zero, 22992 ADDIU $16, $zero, -831 ADDIU $17, $zero, 32529 ADDIU $18,
  //   $zero, 9769 ADDIU $19, $zero, 20136 ADDIU $20, $zero, 17649 ADDIU $21, $zero, -2156 ADDIU $22,
  //   $zero, 12587 ADDIU $23, $zero, 24276 ADDIU $24, $zero, 23439 ADDIU $25, $zero, 7403 ADDIU $26,
  //   $zero, 18200 ADDIU $27, $zero, -8216 ADDIU $28, $zero, -28273 ADDIU $29, $zero, 23504 ADDIU $30,
  //   $zero, 5830 ADDIU $31, $zero, 28659 LBU $2, 32($18) SW $22, 64($18) LBU $23, 160($21) LW $8, 96($8)
  //   LW $7, 96($21) LW $12, 160($6) LB $6, 0($24) SB $3, 96($2) LB $20, 64($31) SW $24, 96($12) LBU $5,
  //   96($17) LW $29, 96($10) SB $21, 0($4) LBU $19, 0($26) LW $4, 32($11) SB $9, 160($7) SB $29, 0($12)
  //   SW $7, 64($9) SB $13, 160($27) LW $6, 96($14) SW $14, 96($1) SB $20, 32($3) LBU $4, 64($21) LB $31,
  //   96($20) LBU $14, 32($17) LB $22, 96($14) SB $30, 32($17) SB $28, 32($12) LB $26, 0($27) LW $20,
  //   64($15) LBU $10, 0($18) LB $20, 64($2) LBU $11, 0($27) LB $8, 0($5) LW $21, 128($3) SB $21, 160($1)
  //   LW $14, 0($18) LBU $26, 0($25) LBU $7, 0($10) LBU $4, 96($26) SB $26, 128($22) SB $23, 128($14) LBU
  //   $23, 96($19) LBU $20, 0($25) SW $24, 32($29) LBU $21, 96($22) LW $14, 0($3) LBU $11, 160($13) SB
  //   $17, 64($28) LB $4, 32($9) SB $27, 32($15) SW $1, 128($17) LBU $29, 0($14) LB $29, 0($25) SW $22,
  //   160($6) SB $14, 128($24) LBU $28, 64($10) SW $10, 96($18) LB $2, 160($11) LB $14, 160($5) LB $27,
  //   64($30) LB $19, 96($24) LW $27, 160($26) SW $22, 0($24) LW $14, 160($3) LBU $15, 32($1) LB $21,
  //   128($18) SW $14, 96($9) LW $21, 128($4) LW $1, 128($19) LBU $13, 160($15) LB $25, 96($13) LBU $20,
  //   0($10) LW $24, 96($13) LBU $21, 0($19) SB $27, 64($23) SB $26, 160($20) LBU $14, 128($14) LW $28,
  //   0($27) SB $13, 96($14) SW $18, 64($6) LBU $25, 32($21) LB $6, 32($15) SW $23, 128($1) LBU $20,
  //   96($30) SB $22, 96($27) SB $7, 96($8) LBU $6, 160($3) SW $13, 96($6) SW $31, 128($24) SB $26, 0($19)
  //   SB $14, 0($19) LBU $17, 96($15) LB $23, 32($9) SW $8, 0($16) LBU $9, 0($31) LB $7, 0($12) SW $19,
  //   64($25) LB $15, 32($17) LB $20, 0($11)
endmodule

module Decode (
  input  [31:0] C_In,
  input  CLK,
  input  WE_in,
  input  [31:0] Word,
  input  [4:0] rW_in,
  output [31:0] A_out,
  output [31:0] LUI_Data_out,
  output [31:0] B_out,
  output [4:0] Sa_out,
  output [31:0] Ctrl_out,
  output WE,
  output LUI_out,
  output [3:0] Op_ALU_out,
  output SLT_out,
  output SLTU_out,
  output [4:0] rW,
  output [4:0] rA,
  output [4:0] rB,
  output MOVN_out,
  output MOVZ_out,
  output Shift_var
);

  wire not_1_out, or_1_out;
  wire [4:0] bit_extender_1_out;
  wire [31:0] bit_extender_3_out, bit_extender_4_out, multiplexer_4_out, registerfile_1_p8;

  not not_1 (not_1_out, CLK);
  assign bit_extender_1_out = {{4{Word[30]}}, Word[30]};  // Bit_Extender bit_extender_1
  Multiplexer #(.width(5), .enable("false")) multiplexer_1 (
    .in0(Word[20:16]), .in1(bit_extender_1_out), .out(rB), .sel(Word[29]));
  assign LUI_Data_out[15:0] = {{15{Word[30]}}, Word[30]};  // Bit_Extender bit_extender_2
  assign bit_extender_3_out = {{16{Word[15]}}, Word[15:0]};  // Bit_Extender bit_extender_3
  assign bit_extender_4_out = {{16{1'b0}}, Word[15:0]};  // Bit_Extender bit_extender_4
  Multiplexer #(.width(5), .enable("false")) multiplexer_2 (
    .in0(Word[15:11]), .in1(Word[20:16]), .out(rW), .sel(or_1_out));
  or or_1 (or_1_out, Word[29], Word[31]);
  Controls controls_1 (
    .Opcode(Word[31:26]), .Funct(Word[5:0]), .WE(WE), .LUI(LUI_out), .Op_ALU(Op_ALU_out), .SLT(SLT_out),
    .SLTU(SLTU_out), .shift_var(Shift_var), .MOVN(MOVN_out), .MOVZ(MOVZ_out));
  // RegisterFile registerfile_1: pin names not known; wires that end beside it: C_In, not_1_out, WE_in, rW_in, Word[25:21], rB, A_out, registerfile_1_p8
  Multiplexer #(.width(32), .enable("false")) multiplexer_3 (
    .in0(registerfile_1_p8), .in1(multiplexer_4_out), .out(B_out), .sel(Word[29]));
  Multiplexer #(.width(32), .enable("false")) multiplexer_4 (
    .in0(bit_extender_3_out), .in1(bit_extender_4_out), .out(multiplexer_4_out), .sel(Word[28]));

  assign Ctrl_out = Word;
  assign LUI_Data_out[31:16] = Word[15:0];
  assign rA = Word[25:21];
  assign Sa_out = Word[10:6];

  // Notes on the sheet:
  //   5-bit 0
endmodule

module Controls (
  input  [5:0] Opcode,
  input  [5:0] Funct,
  output WE,
  output LUI,
  output [3:0] Op_ALU,
  output SLT,
  output SLTU,
  output shift_var,
  output MOVN,
  output MOVZ
);

  wire and_1_out, and_2_out, and_3_out, and_6_out, and_7_out, and_8_out, and_9_out, nand_1_out, nor_1_out,
       nor_2_out, not_1_out, not_2_out, not_3_out, not_4_out, not_7_out, not_8_out, not_9_out, not_10_out,
       not_11_out, or_1_out;
  wire [2:0] not_5_out;
  wire [3:0] multiplexer_1_out;
  wire [3:3] xor_1_out;

  nor nor_1 (nor_1_out, Opcode[3], Opcode[4], Opcode[5]);
  not not_1 (not_1_out, Funct[5]);
  and and_1 (and_1_out, Funct[2], not_2_out);
  not not_2 (not_2_out, Funct[5]);
  or or_1 (or_1_out, Opcode[0], Opcode[1], Opcode[2]);
  and and_2 (and_2_out, not_1_out, Funct[0], Funct[1]);
  not not_3 (not_3_out, Funct[2]);
  xor xor_1 (xor_1_out[3], and_1_out, Funct[2]);
  not not_4 (not_4_out, Opcode[5]);
  nand nand_1 (nand_1_out, nor_1_out, or_1_out);
  and and_3 (and_3_out, not_3_out, Funct[3]);
  not not_5 (not_5_out[0], Funct[4]);
  not not_6 (not_5_out[2], Funct[4]);
  and and_4 (WE, not_4_out, nand_1_out);
  and and_5 (LUI, Opcode[0], Opcode[1], Opcode[2]);
  and and_6 (and_6_out, Opcode[1], not_7_out);
  not not_7 (not_7_out, Opcode[2]);
  Multiplexer #(.width(4), .enable("false")) multiplexer_1 (
    .in0({xor_1_out[3], Funct[1:0], Funct[4]}), .in1({Funct[4], not_5_out[2], Funct[4], not_5_out[0]}),
    .out(multiplexer_1_out), .sel(and_2_out));
  nor nor_2 (nor_2_out, Opcode[0], Opcode[1], Opcode[2], Opcode[4], Opcode[5], Opcode[3]);
  not not_8 (not_8_out, Funct[5]);
  not not_9 (not_9_out, Funct[5]);
  Multiplexer #(.width(4), .enable("false")) multiplexer_2 (
    .in0(multiplexer_1_out), .in1({Opcode[2:0], Opcode[5]}), .out(Op_ALU), .sel(Opcode[3]));
  not not_10 (not_10_out, Funct[0]);
  not not_11 (not_11_out, Opcode[3]);
  and and_7 (and_7_out, not_11_out, and_3_out);
  and and_8 (and_8_out, and_6_out, Opcode[0]);
  and and_9 (and_9_out, Funct[0], and_3_out, nor_2_out);
  and and_10 (shift_var, nor_2_out, and_1_out);
  and and_11 (MOVN, nor_2_out, not_8_out, Funct[0], Funct[3]);
  and and_12 (MOVZ, nor_2_out, not_10_out, Funct[3], not_9_out);
  or or_2 (SLT, and_6_out, and_7_out);
  or or_3 (SLTU, and_8_out, and_9_out);
endmodule

module Execute (
  input  [31:0] A,
  input  [31:0] B,
  input  [31:0] LUI_Data,
  input  LUI,
  input  SLT,
  input  [3:0] Op_ALU,
  input  [4:0] Sa,
  input  SLTU,
  input  [31:0] Word_in,
  input  [4:0] rW,
  input  WE_in,
  input  MOVN_in,
  input  MOVZ_in,
  input  Shift_var,
  output [31:0] C,
  output [4:0] rW_out,
  output WE_out
);

  wire and_1_out, and_2_out, and_3_out, and_4_out, checkzero32_1_out_2, comparator_1_eq, comparator_1_lt,
       comparator_2_eq, comparator_2_lt, multiplexer_5_out, not_1_out, not_2_out, not_3_out, not_4_out,
       or_1_out, or_2_out, xnor_1_out;
  wire [3:0] multiplexer_2_out;
  wire [4:0] multiplexer_3_out;
  wire [31:0] bit_extender_1_out, bit_extender_2_out, mips_alu_1_p5, multiplexer_1_out, multiplexer_4_out,
       multiplexer_6_out;

  assign bit_extender_1_out = {{31{1'b0}}, not_1_out};  // Bit_Extender bit_extender_1
  not not_1 (not_1_out, or_1_out);
  Multiplexer #(.width(32), .enable("false")) multiplexer_1 (
    .in0(B), .in1(bit_extender_1_out), .out(multiplexer_1_out), .sel(or_1_out));
  CheckZero32 checkzero32_1 (.Ain(B), .out_2(checkzero32_1_out_2));
  Multiplexer #(.width(4), .enable("false")) multiplexer_2 (
    .in0(Op_ALU), .in1(Word_in[5:2]), .out(multiplexer_2_out), .sel(or_1_out));
  and and_1 (and_1_out, MOVN_in, not_2_out);
  not not_2 (not_2_out, checkzero32_1_out_2);
  or or_1 (or_1_out, and_1_out, and_2_out);
  and and_2 (and_2_out, checkzero32_1_out_2, MOVZ_in);
  Multiplexer #(.width(5), .enable("false")) multiplexer_3 (
    .in0(Sa), .in1(A[4:0]), .out(multiplexer_3_out), .sel(Shift_var));
  or or_2 (or_2_out, MOVN_in, MOVZ_in);
  // Mips_ALU mips_alu_1: pin names not known; wires that end beside it: A, multiplexer_1_out, multiplexer_2_out, multiplexer_3_out, mips_alu_1_p5
  Comparator #(.width(32)) comparator_1 (
    .a(A), .b(multiplexer_1_out), .eq(comparator_1_eq), .lt(comparator_1_lt));  // open: gt
  Comparator #(.width(32), .mode("unsigned")) comparator_2 (
    .a(A), .b(multiplexer_1_out), .eq(comparator_2_eq), .lt(comparator_2_lt));  // open: gt
  not not_3 (not_3_out, comparator_1_eq);
  not not_4 (not_4_out, comparator_2_eq);
  Multiplexer #(.width(32), .enable("false")) multiplexer_4 (
    .in0(mips_alu_1_p5), .in1(LUI_Data), .out(multiplexer_4_out), .sel(LUI));
  and and_3 (and_3_out, not_3_out, comparator_1_lt);
  and and_4 (and_4_out, not_4_out, comparator_2_lt);
  xnor xnor_1 (xnor_1_out, or_2_out, or_1_out);
  Multiplexer #(.enable("false")) multiplexer_5 (.in0(and_3_out), .in1(and_4_out), .out(multiplexer_5_out), .sel(SLTU));
  Multiplexer #(.width(32), .enable("false")) multiplexer_6 (
    .in0(multiplexer_4_out), .in1(bit_extender_2_out), .out(multiplexer_6_out), .sel(SLT));
  assign bit_extender_2_out = {{31{1'b0}}, multiplexer_5_out};  // Bit_Extender bit_extender_2
  and and_5 (WE_out, WE_in, xnor_1_out);
  Multiplexer #(.width(32), .enable("false")) multiplexer_7 (
    .in0(multiplexer_6_out), .in1(multiplexer_4_out), .out(C), .sel(or_2_out));

  assign rW_out = rW;

  // Notes on the sheet:
  //   SLT
  //   SLTU
endmodule

module Memory (
  input  [31:0] C_in,
  input  CLK,
  input  We_in,
  input  [4:0] rW,
  output [31:0] C_out,
  output [31:0] Data,
  output WE_OUT,
  output [4:0] rW_out
);

  // LCD_Video lcd_video_1: pin names not known; wires that end beside it: CLK, CLK

  assign C_out = C_in;
  assign Data = C_in;
  assign rW_out = rW;
  assign WE_OUT = We_in;
endmodule

module Writeback (
  input  [31:0] C_in,
  input  [31:0] Data,
  input  WE_in,
  input  [4:0] rW,
  output [31:0] C_out,
  output We_out,
  output [4:0] rW_out
);

  Multiplexer #(.width(32), .enable("false")) multiplexer_1 (.in0(C_in), .in1(Data), .out(C_out), .sel(WE_in));

  assign rW_out = rW;
  assign We_out = WE_in;
endmodule

module ID_EX (
  input  [31:0] A_in,
  input  [31:0] LUI_Data_in,
  input  [31:0] B_in,
  input  CLK,
  input  [4:0] Sa_in,
  input  SLT_in,
  input  SLTU_in,
  input  LUI_in,
  input  [31:0] Ctrl_in,
  input  [3:0] Op_ALU_in,
  input  [4:0] rW_in,
  input  [4:0] rA,
  input  [4:0] rB,
  input  WE,
  input  MOVN_in,
  input  MOVZ_in,
  input  Shift_var_in,
  output [31:0] A_out,
  output [31:0] LUI_Data_out,
  output [31:0] B_out,
  output [4:0] Sa_out,
  output SLT_out,
  output SLTU_out,
  output LUI_out,
  output [31:0] Ctrl_out,
  output [3:0] Op_ALU_out,
  output [4:0] rW_out,
  output [4:0] rA_out,
  output [4:0] rB_out,
  output WE_out,
  output MOVN_out,
  output MOVZ_out,
  output Shift_var
);

  Register #(.width(32)) A_reg (.D(A_in), .en(CLK), .clk(CLK), .Q(A_out));  // open: clr
  Register #(.width(32)) LUI_Data_reg (.D(LUI_Data_in), .en(CLK), .clk(CLK), .Q(LUI_Data_out));  // open: clr
  Register #(.width(32)) B_reg (.D(B_in), .en(CLK), .clk(CLK), .Q(B_out));  // open: clr
  Register #(.width(5)) Sa_reg (.D(Sa_in), .en(CLK), .clk(CLK), .Q(Sa_out));  // open: clr
  Register #(.width(1)) SLTU_reg (.D(SLTU_in), .en(CLK), .clk(CLK), .Q(SLTU_out));  // open: clr
  Register #(.width(1)) LUI_reg (.D(LUI_in), .en(CLK), .clk(CLK), .Q(LUI_out));  // open: clr
  Register #(.width(32)) Ctrl_reg (.D(Ctrl_in), .en(CLK), .clk(CLK), .Q(Ctrl_out));  // open: clr
  Register #(.width(4)) Op_ALU_reg (.D(Op_ALU_in), .en(CLK), .clk(CLK), .Q(Op_ALU_out));  // open: clr
  Register #(.width(5)) register_1 (.D(rW_in), .en(CLK), .clk(CLK), .Q(rW_out));  // open: clr
  Register #(.width(5)) register_2 (.D(rA), .en(CLK), .clk(CLK), .Q(rA_out));  // open: clr
  Register #(.width(5)) register_3 (.D(rB), .en(CLK), .clk(CLK), .Q(rB_out));  // open: clr
  Register #(.width(1)) register_4 (.D(WE), .en(CLK), .clk(CLK), .Q(WE_out));  // open: clr
  Register #(.width(1)) register_5 (.D(MOVN_in), .en(CLK), .clk(CLK), .Q(MOVN_out));  // open: clr
  Register #(.width(1)) register_6 (.D(MOVZ_in), .en(CLK), .clk(CLK), .Q(MOVZ_out));  // open: clr
  Register #(.width(1)) register_7 (.D(Shift_var_in), .en(CLK), .clk(CLK), .Q(Shift_var));  // open: clr
  Register #(.width(1)) SLT_reg (.D(SLT_in), .en(CLK), .clk(CLK), .Q(SLT_out));  // open: clr
endmodule

module IF_ID (
  input  [31:0] Word_in,
  input  CLK,
  output [31:0] Word_out
);

  Register #(.width(32)) register_1 (.D(Word_in), .en(CLK), .clk(CLK), .Q(Word_out));  // open: clr
endmodule

module EX_MEM (
  input  CLK,
  input  [31:0] C_in,
  input  [4:0] rW,
  input  WE_in,
  output [31:0] C_out,
  output [4:0] rW_out,
  output WE_out
);

  Register #(.width(32)) register_1 (.D(C_in), .en(CLK), .clk(CLK), .Q(C_out));  // open: clr
  Register #(.width(5)) register_2 (.D(rW), .en(CLK), .clk(CLK), .Q(rW_out));  // open: clr
  Register #(.width(1)) register_3 (.D(WE_in), .en(CLK), .clk(CLK), .Q(WE_out));  // open: clr
endmodule

module MEM_WB (
  input  CLK,
  input  [31:0] C_in,
  input  [31:0] Data_in,
  input  We_in,
  input  [4:0] rW,
  output [31:0] C_out,
  output [31:0] Data_out,
  output We_out,
  output [4:0] rW_out
);

  Register #(.width(32)) register_1 (.D(C_in), .en(CLK), .clk(CLK), .Q(C_out));  // open: clr
  Register #(.width(32)) register_2 (.D(Data_in), .en(CLK), .clk(CLK), .Q(Data_out));  // open: clr
  Register #(.width(1)) register_3 (.D(We_in), .en(CLK), .clk(CLK), .Q(We_out));  // open: clr
  Register #(.width(5)) register_4 (.D(rW), .en(CLK), .clk(CLK), .Q(rW_out));  // open: clr
endmodule

module Forwarding (
  input  [31:0] ID_EX_A,
  input  [31:0] ID_EX_B,
  input  [31:0] EX_MEM_Out,
  input  [31:0] MEM_WB_Out,
  input  [4:0] rA,
  input  [4:0] rB,
  input  [4:0] rD_EX_MEM,
  input  [4:0] rD_MEM_WB,
  input  WE_EX_MEM,
  input  WE_MEM_WB,
  output [31:0] A_out,
  output [31:0] B_out
);

  wire and_1_out, and_2_out, and_3_out, and_4_out, checknot0_1_aout, checknot0_2_aout, checknot0_3_aout,
       checknot0_4_aout, checknot0_5_aout, checknot0_6_aout, not_1_out, not_2_out, not_3_out, not_4_out;
  wire [4:0] xor_1_out, xor_2_out, xor_3_out, xor_4_out;
  wire [31:0] multiplexer_1_out, multiplexer_3_out;

  assign xor_1_out = rA ^ rD_EX_MEM;  // XOR_Gate xor_1, 5 bits wide
  assign xor_2_out = rB ^ rD_EX_MEM;  // XOR_Gate xor_2, 5 bits wide
  assign xor_3_out = rA ^ rD_MEM_WB;  // XOR_Gate xor_3, 5 bits wide
  assign xor_4_out = rB ^ rD_MEM_WB;  // XOR_Gate xor_4, 5 bits wide
  CheckNot0 checknot0_1 (.Ain(xor_1_out), .Aout(checknot0_1_aout));
  not not_1 (not_1_out, checknot0_1_aout);
  not not_2 (not_2_out, checknot0_2_aout);
  CheckNot0 checknot0_2 (.Ain(xor_2_out), .Aout(checknot0_2_aout));
  CheckNot0 checknot0_3 (.Ain(rD_EX_MEM), .Aout(checknot0_3_aout));
  not not_3 (not_3_out, checknot0_4_aout);
  CheckNot0 checknot0_4 (.Ain(xor_3_out), .Aout(checknot0_4_aout));
  not not_4 (not_4_out, checknot0_5_aout);
  CheckNot0 checknot0_5 (.Ain(xor_4_out), .Aout(checknot0_5_aout));
  CheckNot0 checknot0_6 (.Ain(rD_MEM_WB), .Aout(checknot0_6_aout));
  Multiplexer #(.width(32), .enable("false")) multiplexer_1 (
    .in0(ID_EX_A), .in1(MEM_WB_Out), .out(multiplexer_1_out), .sel(and_3_out));
  and and_1 (and_1_out, not_1_out, WE_EX_MEM, checknot0_3_aout);
  and and_2 (and_2_out, not_2_out, WE_EX_MEM, checknot0_3_aout);
  and and_3 (and_3_out, not_3_out, WE_MEM_WB, checknot0_6_aout);
  and and_4 (and_4_out, not_4_out, WE_MEM_WB, checknot0_6_aout);
  Multiplexer #(.width(32), .enable("false")) multiplexer_2 (
    .in0(multiplexer_1_out), .in1(EX_MEM_Out), .out(A_out), .sel(and_1_out));
  Multiplexer #(.width(32), .enable("false")) multiplexer_3 (
    .in0(ID_EX_B), .in1(MEM_WB_Out), .out(multiplexer_3_out), .sel(and_4_out));
  Multiplexer #(.width(32), .enable("false")) multiplexer_4 (
    .in0(multiplexer_3_out), .in1(EX_MEM_Out), .out(B_out), .sel(and_2_out));
endmodule

module CheckNot0 (
  input  [4:0] Ain,
  output Aout
);

  or or_1 (Aout, Ain[0], Ain[1], Ain[2], Ain[3], Ain[4]);
endmodule

module CheckZero32 (
  input  [31:0] Ain,
  output out_2
);

  nor nor_1 (out_2, Ain[0], Ain[1], Ain[2], Ain[3], Ain[4], Ain[5], Ain[6], Ain[7], Ain[8], Ain[9], Ain[10], Ain[11], Ain[12], Ain[13], Ain[14], Ain[15], Ain[17], Ain[18], Ain[19], Ain[20], Ain[21], Ain[22], Ain[23], Ain[24], Ain[25], Ain[26], Ain[27], Ain[28], Ain[29], Ain[30], Ain[31], Ain[16]);
endmodule
